// Digital circuit 4 Bit Buffer.dig as structural Verilog
module _4_Bit_Buffer (
  input  A_in,
  input  B_in,
  input  C_in,
  input  D_in,
  input  WRITE,
  output A_out,
  output B_out,
  output C_out,
  output D_out
);

  Register register_1 (.D(A_in), .C(WRITE), .en(1'b1), .Q(A_out));
  Register register_2 (.D(B_in), .C(WRITE), .en(1'b1), .Q(B_out));
  Register register_3 (.D(C_in), .C(WRITE), .en(1'b1), .Q(C_out));
  Register register_4 (.D(D_in), .C(WRITE), .en(1'b1), .Q(D_out));

  // Notes on the sheet:
  //   A_in: A in
  //   B_in: B in
  //   C_in: C in
  //   D_in: D in
  //   WRITE: WRITE
  //   A_out: A out
  //   B_out: B out
  //   C_out: C out
  //   D_out: D out
endmodule
