// Digital circuit 1 Bit Buffer.dig as structural Verilog
module _1_Bit_Buffer (
  input  ADDR_LINE,
  input  WRITE,
  input  DATA_IN,
  output DATA_OUT
);

  wire nfet_1_d, nfet_1_s, nfet_2_s, nfet_3_s, not_1_out, pfet_2_d, pullup_1_out, pullup_2_out;

  NFET nfet_1 (.G(ADDR_LINE), .D(nfet_1_d), .S(nfet_1_s));
  assign nfet_1_d = WRITE ? not_1_out : 1'bz;  // Driver driver_1
  not not_1 (not_1_out, DATA_IN);
  PullUp pullup_1 (.out(pullup_1_out));
  PFET pfet_1 (.G(pfet_2_d), .S(pullup_1_out), .D(nfet_1_s));
  NFET nfet_2 (.G(pfet_2_d), .D(nfet_1_s), .S(nfet_2_s));
  PullDown pulldown_1 (.out(nfet_2_s));
  PullUp pullup_2 (.out(pullup_2_out));
  LED led_1 (.in(pfet_2_d));
  PFET pfet_2 (.G(nfet_1_s), .S(pullup_2_out), .D(pfet_2_d));
  NFET nfet_3 (.G(nfet_1_s), .D(pfet_2_d), .S(nfet_3_s));
  PullDown pulldown_2 (.out(nfet_3_s));
  NFET nfet_4 (.G(ADDR_LINE), .D(pfet_2_d), .S(DATA_OUT));
  assign DATA_OUT = WRITE ? DATA_IN : 1'bz;  // Driver driver_2

  // Notes on the sheet:
  //   ADDR_LINE: row line 1
  //   {{de Wortleitung 1}}
  //   WRITE: Write Enable
  //   {{de Schreibfreigabe}}
  //   DATA_IN: Data Input {{de Dateneingang}}
  //   DATA_OUT: Data Output {{de Datenausgang}}
endmodule

/* Test case:
WL1 WL0 WE Data D
# write both cells to one
 1   0  1   1   1
 0   1  1   1   1

# check both are one
 1   0  0   0   1
 0   1  0   0   1

# write cell 0 to zero
 1   0  1   0   0

# check
 1   0  0   0   0
 0   1  0   0   1

# write cell 1 to zero
 0   1  1   0   0

# check
 1   0  0   0   0
 0   1  0   0   0

# if no word line is high, output is in high Z state
 0   0  0   x   z
*/
