// Digital circuit 4 Bit Adder.dig as structural Verilog
module _4_Bit_Adder (
  input  A0,
  input  B0,
  input  C0,
  input  D0,
  input  A1,
  input  B1,
  input  C1,
  input  D1,
  input  Cin,
  output A,
  output B,
  output C,
  output D,
  output Cout
);

  wire full_adder_2_cout, full_adder_3_cout, full_adder_4_cout;

  Full_Adder full_adder_1 (.Cin(full_adder_2_cout), .A(A0), .B(A1), .S(A), .Cout(Cout));
  Full_Adder full_adder_2 (.Cin(full_adder_3_cout), .A(B0), .B(B1), .S(B), .Cout(full_adder_2_cout));
  Full_Adder full_adder_3 (.Cin(full_adder_4_cout), .A(C0), .B(C1), .S(C), .Cout(full_adder_3_cout));
  Full_Adder full_adder_4 (.Cin(Cin), .A(D0), .B(D1), .S(D), .Cout(full_adder_4_cout));

  // Notes on the sheet:
  //   A0: A0
  //   B0: B0
  //   C0: C0
  //   D0: D0
  //   B1: B1
  //   C1: C1
  //   D1: D1
  //   A: A
  //   B: B
  //   C: C
  //   D: D
  //   Cout: Cout
endmodule
