// Digital circuit 4 Bit Ram - SRAM - perfeito.dig as structural Verilog
module _4_Bit_Ram___SRAM___perfeito (
  input  WRITE,
  input  A_in,
  input  [1:0] SELETOR,
  input  B_in,
  input  C_in,
  input  D_in,
  output A_out,
  output B_out,
  output C_out,
  output D_out
);

  wire decoder_1_out_0, decoder_1_out_1, decoder_1_out_2, decoder_1_out_3, nfet_1_d, nfet_1_s, nfet_2_s,
       nfet_3_s, nfet_4_s, nfet_5_s, nfet_6_s, nfet_7_s, nfet_8_s, nfet_9_s, nfet_11_s, nfet_13_s, nfet_16_s,
       nfet_17_d, nfet_17_s, nfet_18_s, nfet_19_s, nfet_20_s, nfet_21_s, nfet_22_s, nfet_23_s, nfet_24_s,
       nfet_25_s, nfet_26_s, nfet_27_s, nfet_28_s, nfet_33_d, nfet_33_s, nfet_34_s, nfet_35_s, nfet_36_s,
       nfet_37_s, nfet_38_s, nfet_39_s, nfet_40_s, nfet_41_s, nfet_43_s, nfet_45_s, nfet_48_s, nfet_49_d,
       nfet_49_s, nfet_50_s, nfet_51_s, nfet_52_s, nfet_53_s, nfet_55_s, nfet_57_s, nfet_59_s, not_1_out,
       not_2_out, not_3_out, not_4_out, pfet_5_d, pfet_6_d, pfet_7_d, pfet_8_d, pfet_13_d, pfet_14_d,
       pfet_15_d, pfet_16_d, pfet_21_d, pfet_22_d, pfet_23_d, pfet_24_d, pfet_25_d, pfet_25_s, pfet_27_d,
       pfet_27_s, pfet_29_d, pfet_29_s, pfet_31_d, pfet_31_s, pulldown_25_out, pulldown_26_out,
       pulldown_27_out, pulldown_28_out, pullup_1_out, pullup_2_out, pullup_3_out, pullup_4_out,
       pullup_5_out, pullup_6_out, pullup_7_out, pullup_8_out, pullup_9_out, pullup_10_out, pullup_11_out,
       pullup_12_out, pullup_13_out, pullup_14_out, pullup_15_out, pullup_16_out, pullup_17_out,
       pullup_18_out, pullup_19_out, pullup_20_out, pullup_21_out, pullup_22_out, pullup_23_out,
       pullup_24_out, pullup_25_out, pullup_26_out, pullup_27_out, pullup_28_out;

  Decoder #(.Selector_Bits(2)) decoder_1 (
    .sel(SELETOR), .out_0(decoder_1_out_0), .out_1(decoder_1_out_1), .out_2(decoder_1_out_2),
    .out_3(decoder_1_out_3));
  NFET nfet_1 (.G(decoder_1_out_0), .D(nfet_1_d), .S(nfet_1_s));
  NFET nfet_2 (.G(decoder_1_out_1), .D(nfet_1_d), .S(nfet_2_s));
  NFET nfet_3 (.G(decoder_1_out_2), .D(nfet_1_d), .S(nfet_3_s));
  NFET nfet_4 (.G(decoder_1_out_3), .D(nfet_1_d), .S(nfet_4_s));
  assign nfet_1_d = WRITE ? not_1_out : 1'bz;  // Driver driver_1
  not not_1 (not_1_out, A_in);
  PullUp pullup_1 (.out(pullup_1_out));
  LED led_1 (.in(pfet_5_d));
  PFET pfet_1 (.G(pfet_5_d), .S(pullup_1_out), .D(nfet_1_s));
  NFET nfet_5 (.G(pfet_5_d), .D(nfet_1_s), .S(nfet_5_s));
  PullDown pulldown_1 (.out(nfet_5_s));
  PullUp pullup_2 (.out(pullup_2_out));
  LED led_2 (.in(pfet_6_d));
  PFET pfet_2 (.G(pfet_6_d), .S(pullup_2_out), .D(nfet_2_s));
  NFET nfet_6 (.G(pfet_6_d), .D(nfet_2_s), .S(nfet_6_s));
  PullDown pulldown_2 (.out(nfet_6_s));
  PullUp pullup_3 (.out(pullup_3_out));
  LED led_3 (.in(pfet_7_d));
  PFET pfet_3 (.G(pfet_7_d), .S(pullup_3_out), .D(nfet_3_s));
  NFET nfet_7 (.G(pfet_7_d), .D(nfet_3_s), .S(nfet_7_s));
  PullDown pulldown_3 (.out(nfet_7_s));
  PullUp pullup_4 (.out(pullup_4_out));
  LED led_4 (.in(pfet_8_d));
  PFET pfet_4 (.G(pfet_8_d), .S(pullup_4_out), .D(nfet_4_s));
  NFET nfet_8 (.G(pfet_8_d), .D(nfet_4_s), .S(nfet_8_s));
  PullDown pulldown_4 (.out(nfet_8_s));
  PullUp pullup_5 (.out(pullup_5_out));
  PFET pfet_5 (.G(nfet_1_s), .S(pullup_5_out), .D(pfet_5_d));
  NFET nfet_9 (.G(nfet_1_s), .D(pfet_5_d), .S(nfet_9_s));
  NFET nfet_10 (.G(decoder_1_out_0), .D(pfet_5_d), .S(A_out));
  PullDown pulldown_5 (.out(nfet_9_s));
  PullUp pullup_6 (.out(pullup_6_out));
  PFET pfet_6 (.G(nfet_2_s), .S(pullup_6_out), .D(pfet_6_d));
  NFET nfet_11 (.G(nfet_2_s), .D(pfet_6_d), .S(nfet_11_s));
  NFET nfet_12 (.G(decoder_1_out_1), .D(pfet_6_d), .S(A_out));
  PullDown pulldown_6 (.out(nfet_11_s));
  PullUp pullup_7 (.out(pullup_7_out));
  PFET pfet_7 (.G(nfet_3_s), .S(pullup_7_out), .D(pfet_7_d));
  NFET nfet_13 (.G(nfet_3_s), .D(pfet_7_d), .S(nfet_13_s));
  NFET nfet_14 (.G(decoder_1_out_2), .D(pfet_7_d), .S(A_out));
  PullDown pulldown_7 (.out(nfet_13_s));
  PullUp pullup_8 (.out(pullup_8_out));
  PFET pfet_8 (.G(nfet_4_s), .S(pullup_8_out), .D(pfet_8_d));
  NFET nfet_15 (.G(decoder_1_out_3), .D(pfet_8_d), .S(A_out));
  NFET nfet_16 (.G(nfet_4_s), .D(pfet_8_d), .S(nfet_16_s));
  PullDown pulldown_8 (.out(nfet_16_s));
  assign A_out = WRITE ? A_in : 1'bz;  // Driver driver_2
  NFET nfet_17 (.G(decoder_1_out_0), .D(nfet_17_d), .S(nfet_17_s));
  NFET nfet_18 (.G(decoder_1_out_1), .D(nfet_17_d), .S(nfet_18_s));
  NFET nfet_19 (.G(decoder_1_out_2), .D(nfet_17_d), .S(nfet_19_s));
  NFET nfet_20 (.G(decoder_1_out_3), .D(nfet_17_d), .S(nfet_20_s));
  assign nfet_17_d = WRITE ? not_2_out : 1'bz;  // Driver driver_3
  not not_2 (not_2_out, B_in);
  PullUp pullup_9 (.out(pullup_9_out));
  PFET pfet_9 (.G(pfet_13_d), .S(pullup_9_out), .D(nfet_17_s));
  NFET nfet_21 (.G(pfet_13_d), .D(nfet_17_s), .S(nfet_21_s));
  PullDown pulldown_9 (.out(nfet_21_s));
  PullUp pullup_10 (.out(pullup_10_out));
  PFET pfet_10 (.G(pfet_14_d), .S(pullup_10_out), .D(nfet_18_s));
  NFET nfet_22 (.G(pfet_14_d), .D(nfet_18_s), .S(nfet_22_s));
  PullDown pulldown_10 (.out(nfet_22_s));
  PullUp pullup_11 (.out(pullup_11_out));
  PFET pfet_11 (.G(pfet_15_d), .S(pullup_11_out), .D(nfet_19_s));
  NFET nfet_23 (.G(pfet_15_d), .D(nfet_19_s), .S(nfet_23_s));
  PullDown pulldown_11 (.out(nfet_23_s));
  PullUp pullup_12 (.out(pullup_12_out));
  PFET pfet_12 (.G(pfet_16_d), .S(pullup_12_out), .D(nfet_20_s));
  NFET nfet_24 (.G(pfet_16_d), .D(nfet_20_s), .S(nfet_24_s));
  PullDown pulldown_12 (.out(nfet_24_s));
  PullUp pullup_13 (.out(pullup_13_out));
  LED led_5 (.in(pfet_13_d));
  PFET pfet_13 (.G(nfet_17_s), .S(pullup_13_out), .D(pfet_13_d));
  NFET nfet_25 (.G(nfet_17_s), .D(pfet_13_d), .S(nfet_25_s));
  PullDown pulldown_13 (.out(nfet_25_s));
  PullUp pullup_14 (.out(pullup_14_out));
  LED led_6 (.in(pfet_14_d));
  PFET pfet_14 (.G(nfet_18_s), .S(pullup_14_out), .D(pfet_14_d));
  NFET nfet_26 (.G(nfet_18_s), .D(pfet_14_d), .S(nfet_26_s));
  PullDown pulldown_14 (.out(nfet_26_s));
  PullUp pullup_15 (.out(pullup_15_out));
  LED led_7 (.in(pfet_15_d));
  PFET pfet_15 (.G(nfet_19_s), .S(pullup_15_out), .D(pfet_15_d));
  NFET nfet_27 (.G(nfet_19_s), .D(pfet_15_d), .S(nfet_27_s));
  PullDown pulldown_15 (.out(nfet_27_s));
  PullUp pullup_16 (.out(pullup_16_out));
  LED led_8 (.in(pfet_16_d));
  PFET pfet_16 (.G(nfet_20_s), .S(pullup_16_out), .D(pfet_16_d));
  NFET nfet_28 (.G(nfet_20_s), .D(pfet_16_d), .S(nfet_28_s));
  PullDown pulldown_16 (.out(nfet_28_s));
  NFET nfet_29 (.G(decoder_1_out_0), .D(pfet_13_d), .S(B_out));
  NFET nfet_30 (.G(decoder_1_out_1), .D(pfet_14_d), .S(B_out));
  NFET nfet_31 (.G(decoder_1_out_2), .D(pfet_15_d), .S(B_out));
  NFET nfet_32 (.G(decoder_1_out_3), .D(pfet_16_d), .S(B_out));
  assign B_out = WRITE ? B_in : 1'bz;  // Driver driver_4
  NFET nfet_33 (.G(decoder_1_out_0), .D(nfet_33_d), .S(nfet_33_s));
  NFET nfet_34 (.G(decoder_1_out_1), .D(nfet_33_d), .S(nfet_34_s));
  NFET nfet_35 (.G(decoder_1_out_2), .D(nfet_33_d), .S(nfet_35_s));
  NFET nfet_36 (.G(decoder_1_out_3), .D(nfet_33_d), .S(nfet_36_s));
  assign nfet_33_d = WRITE ? not_3_out : 1'bz;  // Driver driver_5
  not not_3 (not_3_out, C_in);
  PullUp pullup_17 (.out(pullup_17_out));
  LED led_9 (.in(pfet_21_d));
  PFET pfet_17 (.G(pfet_21_d), .S(pullup_17_out), .D(nfet_33_s));
  NFET nfet_37 (.G(pfet_21_d), .D(nfet_33_s), .S(nfet_37_s));
  PullDown pulldown_17 (.out(nfet_37_s));
  PullUp pullup_18 (.out(pullup_18_out));
  LED led_10 (.in(pfet_22_d));
  PFET pfet_18 (.G(pfet_22_d), .S(pullup_18_out), .D(nfet_34_s));
  NFET nfet_38 (.G(pfet_22_d), .D(nfet_34_s), .S(nfet_38_s));
  PullDown pulldown_18 (.out(nfet_38_s));
  PullUp pullup_19 (.out(pullup_19_out));
  LED led_11 (.in(pfet_23_d));
  PFET pfet_19 (.G(pfet_23_d), .S(pullup_19_out), .D(nfet_35_s));
  NFET nfet_39 (.G(pfet_23_d), .D(nfet_35_s), .S(nfet_39_s));
  PullDown pulldown_19 (.out(nfet_39_s));
  PullUp pullup_20 (.out(pullup_20_out));
  LED led_12 (.in(pfet_24_d));
  PFET pfet_20 (.G(pfet_24_d), .S(pullup_20_out), .D(nfet_36_s));
  NFET nfet_40 (.G(pfet_24_d), .D(nfet_36_s), .S(nfet_40_s));
  PullDown pulldown_20 (.out(nfet_40_s));
  PullUp pullup_21 (.out(pullup_21_out));
  PFET pfet_21 (.G(nfet_33_s), .S(pullup_21_out), .D(pfet_21_d));
  NFET nfet_41 (.G(nfet_33_s), .D(pfet_21_d), .S(nfet_41_s));
  NFET nfet_42 (.G(decoder_1_out_0), .D(pfet_21_d), .S(C_out));
  PullDown pulldown_21 (.out(nfet_41_s));
  PullUp pullup_22 (.out(pullup_22_out));
  PFET pfet_22 (.G(nfet_34_s), .S(pullup_22_out), .D(pfet_22_d));
  NFET nfet_43 (.G(nfet_34_s), .D(pfet_22_d), .S(nfet_43_s));
  NFET nfet_44 (.G(decoder_1_out_1), .D(pfet_22_d), .S(C_out));
  PullDown pulldown_22 (.out(nfet_43_s));
  PullUp pullup_23 (.out(pullup_23_out));
  PFET pfet_23 (.G(nfet_35_s), .S(pullup_23_out), .D(pfet_23_d));
  NFET nfet_45 (.G(nfet_35_s), .D(pfet_23_d), .S(nfet_45_s));
  NFET nfet_46 (.G(decoder_1_out_2), .D(pfet_23_d), .S(C_out));
  PullDown pulldown_23 (.out(nfet_45_s));
  PullUp pullup_24 (.out(pullup_24_out));
  PFET pfet_24 (.G(nfet_36_s), .S(pullup_24_out), .D(pfet_24_d));
  NFET nfet_47 (.G(decoder_1_out_3), .D(pfet_24_d), .S(C_out));
  NFET nfet_48 (.G(nfet_36_s), .D(pfet_24_d), .S(nfet_48_s));
  PullDown pulldown_24 (.out(nfet_48_s));
  assign C_out = WRITE ? C_in : 1'bz;  // Driver driver_6
  NFET nfet_49 (.G(decoder_1_out_0), .D(nfet_49_d), .S(nfet_49_s));
  NFET nfet_50 (.G(decoder_1_out_1), .D(nfet_49_d), .S(nfet_50_s));
  NFET nfet_51 (.G(decoder_1_out_2), .D(nfet_49_d), .S(nfet_51_s));
  NFET nfet_52 (.G(decoder_1_out_3), .D(nfet_49_d), .S(nfet_52_s));
  assign nfet_49_d = WRITE ? not_4_out : 1'bz;  // Driver driver_7
  not not_4 (not_4_out, D_in);
  PullUp pullup_25 (.out(pullup_25_out));
  PullDown pulldown_25 (.out(pulldown_25_out));
  PullUp pullup_26 (.out(pullup_26_out));
  PullDown pulldown_26 (.out(pulldown_26_out));
  PullUp pullup_27 (.out(pullup_27_out));
  PullDown pulldown_27 (.out(pulldown_27_out));
  PullUp pullup_28 (.out(pullup_28_out));
  PullDown pulldown_28 (.out(pulldown_28_out));
  LED led_13 (.in(pfet_25_d));
  PFET pfet_25 (.G(nfet_49_s), .S(pfet_25_s), .D(pfet_25_d));
  PFET pfet_26 (.G(pfet_25_d), .S(pullup_25_out), .D(nfet_49_s));
  NFET nfet_53 (.G(nfet_49_s), .D(pfet_25_d), .S(nfet_53_s));
  NFET nfet_54 (.G(pfet_25_d), .D(nfet_49_s), .S(pulldown_25_out));
  LED led_14 (.in(pfet_27_d));
  PFET pfet_27 (.G(nfet_50_s), .S(pfet_27_s), .D(pfet_27_d));
  PFET pfet_28 (.G(pfet_27_d), .S(pullup_26_out), .D(nfet_50_s));
  NFET nfet_55 (.G(nfet_50_s), .D(pfet_27_d), .S(nfet_55_s));
  NFET nfet_56 (.G(pfet_27_d), .D(nfet_50_s), .S(pulldown_26_out));
  LED led_15 (.in(pfet_29_d));
  PFET pfet_29 (.G(nfet_51_s), .S(pfet_29_s), .D(pfet_29_d));
  PFET pfet_30 (.G(pfet_29_d), .S(pullup_27_out), .D(nfet_51_s));
  NFET nfet_57 (.G(nfet_51_s), .D(pfet_29_d), .S(nfet_57_s));
  NFET nfet_58 (.G(pfet_29_d), .D(nfet_51_s), .S(pulldown_27_out));
  LED led_16 (.in(pfet_31_d));
  PFET pfet_31 (.G(nfet_52_s), .S(pfet_31_s), .D(pfet_31_d));
  PFET pfet_32 (.G(pfet_31_d), .S(pullup_28_out), .D(nfet_52_s));
  NFET nfet_59 (.G(nfet_52_s), .D(pfet_31_d), .S(nfet_59_s));
  NFET nfet_60 (.G(pfet_31_d), .D(nfet_52_s), .S(pulldown_28_out));
  PullUp pullup_29 (.out(pfet_25_s));
  NFET nfet_61 (.G(decoder_1_out_0), .D(pfet_25_d), .S(D_out));
  PullDown pulldown_29 (.out(nfet_53_s));
  PullUp pullup_30 (.out(pfet_27_s));
  NFET nfet_62 (.G(decoder_1_out_1), .D(pfet_27_d), .S(D_out));
  PullDown pulldown_30 (.out(nfet_55_s));
  PullUp pullup_31 (.out(pfet_29_s));
  NFET nfet_63 (.G(decoder_1_out_2), .D(pfet_29_d), .S(D_out));
  PullDown pulldown_31 (.out(nfet_57_s));
  PullUp pullup_32 (.out(pfet_31_s));
  NFET nfet_64 (.G(decoder_1_out_3), .D(pfet_31_d), .S(D_out));
  PullDown pulldown_32 (.out(nfet_59_s));
  assign D_out = WRITE ? D_in : 1'bz;  // Driver driver_8

  // Notes on the sheet:
  //   WRITE: Write Enable
  //   {{de Schreibfreigabe}}
  //   A_in: A in
  //   A_out: Data Output {{de Datenausgang}}
  //   SELETOR: SELETOR
  //   B_out: B out
  //   C_out: C out
  //   D_out: D out
  //   B_in: B in
  //   C_in: C in
  //   D_in: D in
endmodule
