// Digital circuit 4 Bit Ram.dig as structural Verilog
module _4_Bit_Ram (
  input  A0,
  input  B0,
  input  C0,
  input  D0,
  input  WRITE,
  input  [1:0] SELETOR,
  output A1,
  output B1,
  output C1,
  output D1
);

  RAMAsync ramasync_1 (.A(SELETOR), .D(A0), .we(WRITE), .Q(A1));
  RAMAsync ramasync_2 (.A(SELETOR), .D(B0), .we(WRITE), .Q(B1));
  RAMAsync ramasync_3 (.A(SELETOR), .D(C0), .we(WRITE), .Q(C1));
  RAMAsync ramasync_4 (.A(SELETOR), .D(D0), .we(WRITE), .Q(D1));

  // Notes on the sheet:
  //   A0: A0
  //   B0: B0
  //   C0: C0
  //   D0: D0
  //   WRITE: WRITE
  //   SELETOR: SELETOR
  //   A1: A1
  //   B1: B1
  //   C1: C1
  //   D1: D1
endmodule
