// Digital circuit Display - b.dig as structural Verilog
module Display___b (
  input  B_2,
  input  C,
  input  D,
  output b
);

  wire and_1_out, and_2_out, not_1_out, not_2_out, not_3_out;

  not not_1 (not_1_out, B_2);
  not not_2 (not_2_out, C);
  not not_3 (not_3_out, D);
  and and_1 (and_1_out, not_2_out, not_3_out);
  and and_2 (and_2_out, C, D);
  or or_1 (b, not_1_out, and_1_out, and_2_out);

  // Notes on the sheet:
  //   b: b
endmodule
