// Digital circuit Display - d.dig as structural Verilog
module Display___d (
  input  A,
  input  B,
  input  C,
  input  D_2,
  output d
);

  wire and_1_out, and_2_out, and_3_out, and_4_out, not_1_out, not_2_out, not_3_out;

  not not_1 (not_1_out, B);
  not not_2 (not_2_out, C);
  not not_3 (not_3_out, D_2);
  and and_1 (and_1_out, not_1_out, not_3_out);
  and and_2 (and_2_out, B, not_2_out, D_2);
  and and_3 (and_3_out, not_1_out, C);
  and and_4 (and_4_out, C, not_3_out);
  or or_1 (d, A, and_1_out, and_2_out, and_3_out, and_4_out);

  // Notes on the sheet:
  //   d: d
endmodule
