// Digital circuit Display - e.dig as structural Verilog
module Display___e (
  input  B,
  input  C,
  input  D,
  output e
);

  wire and_1_out, and_2_out, not_1_out, not_2_out;

  not not_1 (not_1_out, B);
  not not_2 (not_2_out, D);
  and and_1 (and_1_out, not_1_out, not_2_out);
  and and_2 (and_2_out, C, not_2_out);
  or or_1 (e, and_1_out, and_2_out);

  // Notes on the sheet:
  //   e: e
endmodule
