// Digital circuit Exercicio 1.dig as structural Verilog
module Exercicio_1 (
  input  [1:0] Seletor,
  input  in_7,
  input  in_8,
  input  in_9,
  input  in_10,
  input  in_11,
  input  in_12,
  input  in_13,
  output A,
  output B,
  output C,
  output D,
  output out_6
);

  wire _4_bit_adder_1_a, _4_bit_adder_1_b, _4_bit_adder_1_c, _4_bit_adder_1_d, _4_bit_buffer_1_a_out,
       _4_bit_buffer_1_b_out, _4_bit_buffer_1_c_out, _4_bit_buffer_1_d_out, _4_bit_buffer_2_a_out,
       _4_bit_buffer_2_b_out, _4_bit_buffer_2_c_out, _4_bit_buffer_2_d_out, _4_bit_buffer_3_a_out,
       _4_bit_buffer_3_b_out, _4_bit_buffer_3_c_out, _4_bit_buffer_3_d_out, _4_bit_buffer_4_a_out,
       _4_bit_buffer_4_b_out, _4_bit_buffer_4_c_out, _4_bit_buffer_4_d_out, _4_bit_buffer_5_a_out,
       _4_bit_buffer_5_b_out, _4_bit_buffer_5_c_out, _4_bit_buffer_5_d_out, display___decoder_1_a_2,
       display___decoder_1_b_2, display___decoder_1_c_2, display___decoder_1_d_2, display___decoder_1_e,
       display___decoder_1_f, display___decoder_1_g, rom___4_bits_1_a, rom___4_bits_1_b, rom___4_bits_1_c,
       rom___4_bits_1_d;

  ROM___4_bits rom___4_bits_1 (
    .Seletor(Seletor), .A(rom___4_bits_1_a), .B(rom___4_bits_1_b), .C(rom___4_bits_1_c), .D(rom___4_bits_1_d));
  _4_Bit_Buffer _4_bit_buffer_1 (
    .A_in(rom___4_bits_1_a), .B_in(rom___4_bits_1_b), .C_in(rom___4_bits_1_c), .D_in(rom___4_bits_1_d),
    .WRITE(in_7), .A_out(_4_bit_buffer_1_a_out), .B_out(_4_bit_buffer_1_b_out),
    .C_out(_4_bit_buffer_1_c_out), .D_out(_4_bit_buffer_1_d_out));
  assign D = in_12 ? _4_bit_buffer_1_d_out : 1'bz;  // Driver driver_1
  assign C = in_12 ? _4_bit_buffer_1_c_out : 1'bz;  // Driver driver_2
  _4_Bit_Buffer _4_bit_buffer_2 (
    .A_in(A), .B_in(B), .C_in(C), .D_in(D), .WRITE(in_8), .A_out(_4_bit_buffer_2_a_out),
    .B_out(_4_bit_buffer_2_b_out), .C_out(_4_bit_buffer_2_c_out), .D_out(_4_bit_buffer_2_d_out));
  assign B = in_12 ? _4_bit_buffer_1_b_out : 1'bz;  // Driver driver_3
  assign A = in_12 ? _4_bit_buffer_1_a_out : 1'bz;  // Driver driver_4
  _4_Bit_Buffer _4_bit_buffer_3 (
    .A_in(A), .B_in(B), .C_in(C), .D_in(D), .WRITE(in_9), .A_out(_4_bit_buffer_3_a_out),
    .B_out(_4_bit_buffer_3_b_out), .C_out(_4_bit_buffer_3_c_out), .D_out(_4_bit_buffer_3_d_out));
  _4_Bit_Adder _4_bit_adder_1 (
    .A0(_4_bit_buffer_2_a_out), .B0(_4_bit_buffer_2_b_out), .C0(_4_bit_buffer_2_c_out),
    .D0(_4_bit_buffer_2_d_out), .A1(_4_bit_buffer_3_a_out), .B1(_4_bit_buffer_3_b_out),
    .C1(_4_bit_buffer_3_c_out), .D1(_4_bit_buffer_3_d_out), .Cin(1'b0), .A(_4_bit_adder_1_a),
    .B(_4_bit_adder_1_b), .C(_4_bit_adder_1_c), .D(_4_bit_adder_1_d), .Cout(out_6));
  _4_Bit_Buffer _4_bit_buffer_4 (
    .A_in(A), .B_in(B), .C_in(C), .D_in(D), .WRITE(in_10), .A_out(_4_bit_buffer_4_a_out),
    .B_out(_4_bit_buffer_4_b_out), .C_out(_4_bit_buffer_4_c_out), .D_out(_4_bit_buffer_4_d_out));
  _4_Bit_Buffer _4_bit_buffer_5 (
    .A_in(_4_bit_adder_1_a), .B_in(_4_bit_adder_1_b), .C_in(_4_bit_adder_1_c), .D_in(_4_bit_adder_1_d),
    .WRITE(in_11), .A_out(_4_bit_buffer_5_a_out), .B_out(_4_bit_buffer_5_b_out),
    .C_out(_4_bit_buffer_5_c_out), .D_out(_4_bit_buffer_5_d_out));
  assign A = in_13 ? _4_bit_buffer_5_a_out : 1'bz;  // Driver driver_5
  assign B = in_13 ? _4_bit_buffer_5_b_out : 1'bz;  // Driver driver_6
  Display___Decoder display___decoder_1 (
    .A(_4_bit_buffer_4_a_out), .B(_4_bit_buffer_4_b_out), .C(_4_bit_buffer_4_c_out),
    .D(_4_bit_buffer_4_d_out), .g(display___decoder_1_g), .f(display___decoder_1_f),
    .e(display___decoder_1_e), .d_2(display___decoder_1_d_2), .c_2(display___decoder_1_c_2),
    .b_2(display___decoder_1_b_2), .a_2(display___decoder_1_a_2));
  assign C = in_13 ? _4_bit_buffer_5_c_out : 1'bz;  // Driver driver_7
  assign D = in_13 ? _4_bit_buffer_5_d_out : 1'bz;  // Driver driver_8
  Seven_Seg seven_seg_1 (
    .a(display___decoder_1_a_2), .b(display___decoder_1_b_2), .c(display___decoder_1_c_2),
    .d(display___decoder_1_d_2), .e(display___decoder_1_e), .f(display___decoder_1_f),
    .g(display___decoder_1_g), .dp(1'b0));

  // Notes on the sheet:
  //   A: A
  //   B: B
  //   C: C
  //   D: D
endmodule
