// Digital circuit Exercicio 2.dig as structural Verilog
module Exercicio_2 (
  input  [1:0] Seletor,
  input  WRITE_BUFFER,
  input  WRITE_BUFFER_2,
  input  WRITE_BUFFER_3,
  input  WRITE_BUFFER_4,
  input  WRITE_BUFFER_5,
  input  WRITE_BARRAMENTO,
  input  WRITE_BARRAMENTO_2,
  input  WRITE,
  input  A_in,
  input  B_in,
  input  C_in,
  input  D_in,
  input  WRITE_BARRAMENTO_3,
  input  WRITE_BUFFER_6,
  output A,
  output B,
  output C,
  output D,
  output out_6
);

  wire _4_bit_adder_1_a, _4_bit_adder_1_b, _4_bit_adder_1_c, _4_bit_adder_1_d, _4_bit_buffer_1_a_out,
       _4_bit_buffer_1_b_out, _4_bit_buffer_1_c_out, _4_bit_buffer_1_d_out, _4_bit_buffer_2_a_out,
       _4_bit_buffer_2_b_out, _4_bit_buffer_2_c_out, _4_bit_buffer_2_d_out, _4_bit_buffer_3_a_out,
       _4_bit_buffer_3_b_out, _4_bit_buffer_3_c_out, _4_bit_buffer_3_d_out, _4_bit_buffer_4_a_out,
       _4_bit_buffer_4_b_out, _4_bit_buffer_4_c_out, _4_bit_buffer_4_d_out, _4_bit_buffer_5_a_out,
       _4_bit_buffer_5_b_out, _4_bit_buffer_5_c_out, _4_bit_buffer_5_d_out, _4_bit_buffer_6_a_out,
       _4_bit_buffer_6_b_out, _4_bit_buffer_6_c_out, _4_bit_buffer_6_d_out, _4_bit_ram_1_a1, _4_bit_ram_1_b1,
       _4_bit_ram_1_c1, _4_bit_ram_1_d1, display___decoder_1_a_2, display___decoder_1_b_2,
       display___decoder_1_c_2, display___decoder_1_d_2, display___decoder_1_e, display___decoder_1_f,
       display___decoder_1_g;

  _4_Bit_Ram _4_bit_ram_1 (
    .A0(A), .B0(B), .C0(C), .D0(D), .WRITE(WRITE), .SELETOR(Seletor), .A1(_4_bit_ram_1_a1),
    .B1(_4_bit_ram_1_b1), .C1(_4_bit_ram_1_c1), .D1(_4_bit_ram_1_d1));
  _4_Bit_Buffer _4_bit_buffer_1 (
    .A_in(_4_bit_ram_1_a1), .B_in(_4_bit_ram_1_b1), .C_in(_4_bit_ram_1_c1), .D_in(_4_bit_ram_1_d1),
    .WRITE(WRITE_BUFFER), .A_out(_4_bit_buffer_1_a_out), .B_out(_4_bit_buffer_1_b_out),
    .C_out(_4_bit_buffer_1_c_out), .D_out(_4_bit_buffer_1_d_out));
  assign D = WRITE_BARRAMENTO ? _4_bit_buffer_1_d_out : 1'bz;  // Driver driver_1
  assign C = WRITE_BARRAMENTO ? _4_bit_buffer_1_c_out : 1'bz;  // Driver driver_2
  _4_Bit_Buffer _4_bit_buffer_2 (
    .A_in(A), .B_in(B), .C_in(C), .D_in(D), .WRITE(WRITE_BUFFER_2), .A_out(_4_bit_buffer_2_a_out),
    .B_out(_4_bit_buffer_2_b_out), .C_out(_4_bit_buffer_2_c_out), .D_out(_4_bit_buffer_2_d_out));
  assign B = WRITE_BARRAMENTO ? _4_bit_buffer_1_b_out : 1'bz;  // Driver driver_3
  assign A = WRITE_BARRAMENTO ? _4_bit_buffer_1_a_out : 1'bz;  // Driver driver_4
  _4_Bit_Buffer _4_bit_buffer_3 (
    .A_in(A_in), .B_in(B_in), .C_in(C_in), .D_in(D_in), .WRITE(WRITE_BUFFER_6),
    .A_out(_4_bit_buffer_3_a_out), .B_out(_4_bit_buffer_3_b_out), .C_out(_4_bit_buffer_3_c_out),
    .D_out(_4_bit_buffer_3_d_out));
  assign A = WRITE_BARRAMENTO_3 ? _4_bit_buffer_3_a_out : 1'bz;  // Driver driver_5
  assign B = WRITE_BARRAMENTO_3 ? _4_bit_buffer_3_b_out : 1'bz;  // Driver driver_6
  _4_Bit_Buffer _4_bit_buffer_4 (
    .A_in(A), .B_in(B), .C_in(C), .D_in(D), .WRITE(WRITE_BUFFER_3), .A_out(_4_bit_buffer_4_a_out),
    .B_out(_4_bit_buffer_4_b_out), .C_out(_4_bit_buffer_4_c_out), .D_out(_4_bit_buffer_4_d_out));
  assign C = WRITE_BARRAMENTO_3 ? _4_bit_buffer_3_c_out : 1'bz;  // Driver driver_7
  assign D = WRITE_BARRAMENTO_3 ? _4_bit_buffer_3_d_out : 1'bz;  // Driver driver_8
  _4_Bit_Adder _4_bit_adder_1 (
    .A0(_4_bit_buffer_2_a_out), .B0(_4_bit_buffer_2_b_out), .C0(_4_bit_buffer_2_c_out),
    .D0(_4_bit_buffer_2_d_out), .A1(_4_bit_buffer_4_a_out), .B1(_4_bit_buffer_4_b_out),
    .C1(_4_bit_buffer_4_c_out), .D1(_4_bit_buffer_4_d_out), .Cin(1'b0), .A(_4_bit_adder_1_a),
    .B(_4_bit_adder_1_b), .C(_4_bit_adder_1_c), .D(_4_bit_adder_1_d), .Cout(out_6));
  _4_Bit_Buffer _4_bit_buffer_5 (
    .A_in(_4_bit_adder_1_a), .B_in(_4_bit_adder_1_b), .C_in(_4_bit_adder_1_c), .D_in(_4_bit_adder_1_d),
    .WRITE(WRITE_BUFFER_5), .A_out(_4_bit_buffer_5_a_out), .B_out(_4_bit_buffer_5_b_out),
    .C_out(_4_bit_buffer_5_c_out), .D_out(_4_bit_buffer_5_d_out));
  assign A = WRITE_BARRAMENTO_2 ? _4_bit_buffer_5_a_out : 1'bz;  // Driver driver_9
  assign B = WRITE_BARRAMENTO_2 ? _4_bit_buffer_5_b_out : 1'bz;  // Driver driver_10
  assign C = WRITE_BARRAMENTO_2 ? _4_bit_buffer_5_c_out : 1'bz;  // Driver driver_11
  assign D = WRITE_BARRAMENTO_2 ? _4_bit_buffer_5_d_out : 1'bz;  // Driver driver_12
  _4_Bit_Buffer _4_bit_buffer_6 (
    .A_in(A), .B_in(B), .C_in(C), .D_in(D), .WRITE(WRITE_BUFFER_4), .A_out(_4_bit_buffer_6_a_out),
    .B_out(_4_bit_buffer_6_b_out), .C_out(_4_bit_buffer_6_c_out), .D_out(_4_bit_buffer_6_d_out));
  Display___Decoder display___decoder_1 (
    .A(_4_bit_buffer_6_a_out), .B(_4_bit_buffer_6_b_out), .C(_4_bit_buffer_6_c_out),
    .D(_4_bit_buffer_6_d_out), .g(display___decoder_1_g), .f(display___decoder_1_f),
    .e(display___decoder_1_e), .d_2(display___decoder_1_d_2), .c_2(display___decoder_1_c_2),
    .b_2(display___decoder_1_b_2), .a_2(display___decoder_1_a_2));
  Seven_Seg seven_seg_1 (
    .a(display___decoder_1_a_2), .b(display___decoder_1_b_2), .c(display___decoder_1_c_2),
    .d(display___decoder_1_d_2), .e(display___decoder_1_e), .f(display___decoder_1_f),
    .g(display___decoder_1_g), .dp(1'b0));

  // Notes on the sheet:
  //   A: A
  //   B: B
  //   C: C
  //   D: D
  //   WRITE_BUFFER: WRITE BUFFER
  //   WRITE_BUFFER_2: WRITE BUFFER
  //   WRITE_BUFFER_3: WRITE BUFFER
  //   WRITE_BUFFER_4: WRITE BUFFER
  //   WRITE_BUFFER_5: WRITE BUFFER
  //   WRITE_BARRAMENTO: WRITE BARRAMENTO
  //   WRITE_BARRAMENTO_2: WRITE BARRAMENTO
  //   WRITE: WRITE
  //   A_in: A in
  //   B_in: B in
  //   WRITE_BARRAMENTO_3: WRITE BARRAMENTO
  //   WRITE_BUFFER_6: WRITE BUFFER
endmodule
