// Digital circuit Full Adder.dig as structural Verilog
module Full_Adder (
  input  Cin,
  input  A,
  input  B,
  output S,
  output Cout
);

  wire and_1_out, and_2_out, and_3_out;

  xor xor_1 (S, Cin, A, B);
  and and_1 (and_1_out, A, B);
  and and_2 (and_2_out, Cin, A);
  and and_3 (and_3_out, Cin, B);
  or or_1 (Cout, and_1_out, and_2_out, and_3_out);

  // Notes on the sheet:
  //   Cin: Cin
  //   A: A
  //   B: B
  //   S: S
  //   Cout: Cout
endmodule
