// Digital circuit RAM.dig as structural Verilog
module RAM (
  input  ADDR,
  input  DADOS,
  output out_3
);

  wire nfet_1_d, nfet_4_s, not_1_out;

  NFET nfet_1 (.G(ADDR), .D(nfet_1_d), .S(DADOS));
  NFET nfet_2 (.G(nfet_4_s), .D(nfet_1_d), .S(1'b1));
  NFET nfet_3 (.G(nfet_4_s), .D(1'b0), .S(nfet_1_d));
  not not_1 (not_1_out, DADOS);
  NFET nfet_4 (.G(nfet_1_d), .D(1'b1), .S(nfet_4_s));
  NFET nfet_5 (.G(nfet_1_d), .D(nfet_4_s), .S(1'b0));
  NFET nfet_6 (.G(ADDR), .D(not_1_out), .S(nfet_4_s));

  assign out_3 = DADOS;

  // Notes on the sheet:
  //   ADDR: ADDR
  //   DADOS: DADOS
endmodule
