// Digital circuit ROM - 4 bits.dig as structural Verilog
module ROM___4_bits (
  input  [1:0] Seletor,
  output A,
  output B,
  output C,
  output D
);

  wire decoder_1_out_0, decoder_1_out_1, decoder_1_out_2, decoder_1_out_3;

  Decoder #(.Selector_Bits(2)) decoder_1 (
    .sel(Seletor), .out_0(decoder_1_out_0), .out_1(decoder_1_out_1), .out_2(decoder_1_out_2),
    .out_3(decoder_1_out_3));
  PullDown pulldown_1 (.out(A));
  DiodeForward #(.Blown("true")) diodeforward_1 (.in(decoder_1_out_0), .out(A));
  DiodeForward #(.Blown("true")) diodeforward_2 (.in(decoder_1_out_1), .out(A));
  DiodeForward #(.Blown("true")) diodeforward_3 (.in(decoder_1_out_2), .out(A));
  DiodeForward #(.Blown("true")) diodeforward_4 (.in(decoder_1_out_3), .out(A));
  PullDown pulldown_2 (.out(B));
  DiodeForward #(.Blown("true")) diodeforward_5 (.in(decoder_1_out_0), .out(B));
  DiodeForward #(.Blown("true")) diodeforward_6 (.in(decoder_1_out_1), .out(B));
  DiodeForward #(.Blown("true")) diodeforward_7 (.in(decoder_1_out_2), .out(B));
  DiodeForward #(.Blown("true")) diodeforward_8 (.in(decoder_1_out_3), .out(B));
  PullDown pulldown_3 (.out(C));
  DiodeForward #(.Blown("true")) diodeforward_9 (.in(decoder_1_out_0), .out(C));
  DiodeForward #(.Blown("true")) diodeforward_10 (.in(decoder_1_out_1), .out(C));
  DiodeForward diodeforward_11 (.in(decoder_1_out_2), .out(C));
  DiodeForward diodeforward_12 (.in(decoder_1_out_3), .out(C));
  PullDown pulldown_4 (.out(D));
  DiodeForward #(.Blown("true")) diodeforward_13 (.in(decoder_1_out_0), .out(D));
  DiodeForward diodeforward_14 (.in(decoder_1_out_1), .out(D));
  DiodeForward #(.Blown("true")) diodeforward_15 (.in(decoder_1_out_2), .out(D));
  DiodeForward diodeforward_16 (.in(decoder_1_out_3), .out(D));

  // Notes on the sheet:
  //   Seletor: Seletor
  //   A: A
  //   B: B
  //   C: C
  //   D: D
endmodule
