// Digital circuit Display - Decoder.dig as structural Verilog
module Display___Decoder (
  input  A,
  input  B,
  input  C,
  input  D,
  output g,
  output f,
  output e,
  output d_2,
  output c_2,
  output b_2,
  output a_2
);

  Display___a display___a_1 (.A_2(A), .B(B), .C(C), .D(D), .a(a_2));
  Display___b display___b_1 (.B_2(B), .C(C), .D(D), .b(b_2));
  Display___c display___c_1 (.B(B), .C_2(C), .D(D), .c(c_2));
  Display___d display___d_1 (.A(A), .B(B), .C(C), .D_2(D), .d(d_2));
  Display___e display___e_1 (.B(B), .C(C), .D(D), .e(e));
  Display___f display___f_1 (.A(A), .B(B), .C(C), .D(D), .f(f));
  Display___g display___g_1 (.A(A), .B(B), .C(C), .D(D), .g(g));

  // Notes on the sheet:
  //   A: A
  //   B: B
  //   C: C
  //   D: D
  //   g: g
  //   f: f
  //   e: e
  //   d_2: d
  //   c_2: c
  //   b_2: b
  //   a_2: a
endmodule
