// Digital circuit Display - a.dig as structural Verilog
module Display___a (
  input  A_2,
  input  B,
  input  C,
  input  D,
  output a
);

  wire and_1_out, and_2_out, not_1_out, not_2_out;

  not not_1 (not_1_out, B);
  not not_2 (not_2_out, D);
  and and_1 (and_1_out, B, D);
  and and_2 (and_2_out, not_1_out, not_2_out);
  or or_1 (a, A_2, and_1_out, and_2_out, C);

  // Notes on the sheet:
  //   a: a
endmodule
