// Digital circuit Display - c.dig as structural Verilog
module Display___c (
  input  B,
  input  C_2,
  input  D,
  output c
);

  wire not_1_out;

  not not_1 (not_1_out, C_2);
  or or_1 (c, B, not_1_out, D);

  // Notes on the sheet:
  //   c: c
endmodule
