// Digital circuit Display - f.dig as structural Verilog
module Display___f (
  input  A,
  input  B,
  input  C,
  input  D,
  output f
);

  wire and_1_out, and_2_out, and_3_out, not_1_out, not_2_out;

  not not_1 (not_1_out, C);
  not not_2 (not_2_out, D);
  and and_1 (and_1_out, B, not_1_out);
  and and_2 (and_2_out, B, not_2_out);
  and and_3 (and_3_out, not_1_out, not_2_out);
  or or_1 (f, A, and_1_out, and_2_out, and_3_out);

  // Notes on the sheet:
  //   f: f
endmodule
