// Digital circuit ROM - 4 bits.dig as structural Verilog
module ROM___4_bits (
  input  [1:0] Seletor,
  output Bit_2,
  output Bit_2_2,
  output Bit_1,
  output Bit_0
);

  wire decoder_1_out_0, decoder_1_out_1, decoder_1_out_2, decoder_1_out_3;

  Decoder #(.Selector_Bits(2)) decoder_1 (
    .sel(Seletor), .out_0(decoder_1_out_0), .out_1(decoder_1_out_1), .out_2(decoder_1_out_2),
    .out_3(decoder_1_out_3));
  PullDown pulldown_1 (.out(Bit_2));
  DiodeForward diodeforward_1 (.in(decoder_1_out_0), .out(Bit_2));
  DiodeForward diodeforward_2 (.in(decoder_1_out_1), .out(Bit_2));
  DiodeForward diodeforward_3 (.in(decoder_1_out_2), .out(Bit_2));
  DiodeForward diodeforward_4 (.in(decoder_1_out_3), .out(Bit_2));
  PullDown pulldown_2 (.out(Bit_2_2));
  DiodeForward diodeforward_5 (.in(decoder_1_out_0), .out(Bit_2_2));
  DiodeForward diodeforward_6 (.in(decoder_1_out_1), .out(Bit_2_2));
  DiodeForward diodeforward_7 (.in(decoder_1_out_2), .out(Bit_2_2));
  DiodeForward diodeforward_8 (.in(decoder_1_out_3), .out(Bit_2_2));
  PullDown pulldown_3 (.out(Bit_1));
  DiodeForward diodeforward_9 (.in(decoder_1_out_0), .out(Bit_1));
  DiodeForward diodeforward_10 (.in(decoder_1_out_1), .out(Bit_1));
  DiodeForward #(.Blown("true")) diodeforward_11 (.in(decoder_1_out_2), .out(Bit_1));
  DiodeForward #(.Blown("true")) diodeforward_12 (.in(decoder_1_out_3), .out(Bit_1));
  PullDown pulldown_4 (.out(Bit_0));
  DiodeForward diodeforward_13 (.in(decoder_1_out_0), .out(Bit_0));
  DiodeForward #(.Blown("true")) diodeforward_14 (.in(decoder_1_out_1), .out(Bit_0));
  DiodeForward diodeforward_15 (.in(decoder_1_out_2), .out(Bit_0));
  DiodeForward #(.Blown("true")) diodeforward_16 (.in(decoder_1_out_3), .out(Bit_0));

  // Notes on the sheet:
  //   Seletor: Seletor
  //   Bit_2: Bit 2
  //   Bit_2_2: Bit 1
  //   Bit_1: Bit 1
  //   Bit_0: Bit 0
endmodule
